# Fritzing sketch Equilibrist_Robot (saved by Fritzing 0.9.3b)
breadboards: 1

parts:
  GY2 = MPU-6050 Board GY-521 [form="♀ (female)" package=THT]
  M2 = DC Motor
  Power_plug1 = Power plug
  VCC1 = Battery block 9V
  Part3 = Arduino Uno (Rev3)
  Part2 = Bluetooth HC-05 Macho
  S1 = H-Bridge with L298N
  M1 = DC Motor
  R1 = Resistor [tolerance=±5% resistance=220 package="1206 [SMD]"]
  R2 = Resistor [tolerance=±5% resistance=220 package="2512 [SMD]"]

nets:
  3V3: GY2.pin1, Part3.3V3, Part3.5V, Part2.VCC
  GND: GY2.pin2, Part3.GND, Part2.GND, R2.Pin_1
  N1: GY2.pin3, Part3.A5/SCL
  N2: GY2.pin4, Part3.A4/SDA
  N3: GY2.pin8, Part3.D2
  N4: M2.pin_1, S1.OUT1-Motor1
  N5: M2.pin_2, S1.OUT2-Motor1
  GND_2: Power_plug1.GND, VCC1.-, S1.GND
  N6: VCC1.+, S1.12V
  N7: Part3.D8, S1.IN2
  N8: Part3.D11_PWM/MOSI, Part2.TXD
  N9: Part3.D12/MISO, S1.IN4
  N10: Part3.D4, R1.Pin_0
  N11: Part3.D5_PWM, S1.IN1
  N12: Part3.D6_PWM, S1.IN3
  N13: S1.OUT3-Motor2, M1.pin_2
  N14: S1.OUT4-Motor2, M1.pin_1
  N15: R1.Pin_1, R2.Pin_0

notes:
  3.3V line
  5V line
  9V line
  MPU-6050
  Driver Motor
  Ponte-H L298N
  HC-05 Bluetooh Module
  Battery
  Motor
  Divisor de Tensão

custom parts:
  MPU-6050 Board GY-521: Acelerometro y Giroscopio MPU-6050 Board GY-521
  H-Bridge with L298N: h-bridge
